# Fritzing sketch OtomatoneMouthWiring (saved by Fritzing 0.9.10b)
breadboards: 1

parts:
  SAMD1 = XIAO SAMD21(Seeeduino) [package="DIP (Dual Inline) [THT]"]
  R1 = Slide Potentiometer [maximum_resistance=1kΩ knob_status=50% power=0.5W]
  R2 = Slide Potentiometer [maximum_resistance=1kΩ knob_status=50% power=0.5W]

nets:
  N1: SAMD1.GND, R1.leg2, R2.leg1
  N2: R1.leg1, R2.leg2

notes:
  Mouth Linear Pots

custom parts:
  XIAO SAMD21(Seeeduino): XIAO SAMD21 powered by Microchip SAMD21G18 chip is an ultra-small, high-performance universal development board, the pioneering product of the XIAO series. It supports Arduino / Micropython / CircuitPython development, which is the perfect microcontroller for you to get started with electronics.
