# Fritzing sketch OtomatoneNeckWiring (saved by Fritzing 0.9.10b)
breadboards: 1

parts:
  R3 = Slide Potentiometer [maximum_resistance=100kΩ knob_status=50% power=0.5W]
  R4 = Resistor [tolerance=±5% power=0.25 resistance=100k package=THT]
  SAMD1 = XIAO SAMD21(Seeeduino) [package="DIP (Dual Inline) [THT]"]
  R5 = Resistor [tolerance=±5% power=0.25 resistance=22k package=THT]

nets:
  N1: R3.wiper, SAMD1.D0
  N2: R4.Pin_1, SAMD1.GND, R5.Pin_1

notes:
  Neck Slide Rheostat
  120K Ohm

custom parts:
  XIAO SAMD21(Seeeduino): XIAO SAMD21 powered by Microchip SAMD21G18 chip is an ultra-small, high-performance universal development board, the pioneering product of the XIAO series. It supports Arduino / Micropython / CircuitPython development, which is the perfect microcontroller for you to get started with electronics.
