# Fritzing sketch OtomatoneSelectionSwitchWiring (saved by Fritzing 0.9.10b)
breadboards: 1

parts:
  SAMD1 = XIAO SAMD21(Seeeduino) [package="DIP (Dual Inline) [THT]"]
  S6 = SWITCH-SP3T [package=switch-sp3t-smd]
  R1 = Resistor [tolerance=±5% resistance=10k package="1206 [SMD]"]
  R2 = Resistor [tolerance=±5% resistance=10k package="1206 [SMD]"]
  R3 = Resistor [tolerance=±5% resistance=10k package="1206 [SMD]"]

nets:
  N1: SAMD1.GND, S6.3
  N2: S6.4, R1.Pin_0
  N3: R1.Pin_1, R2.Pin_1, R3.Pin_1

notes:
  Selection Switch
  Brown Wire is the Wiper

custom parts:
  XIAO SAMD21(Seeeduino): XIAO SAMD21 powered by Microchip SAMD21G18 chip is an ultra-small, high-performance universal development board, the pioneering product of the XIAO series. It supports Arduino / Micropython / CircuitPython development, which is the perfect microcontroller for you to get started with electronics.
