# Fritzing sketch OtomatoneVolumePotWiring (saved by Fritzing 0.9.10b)
breadboards: 1

parts:
  SAMD1 = XIAO SAMD21(Seeeduino) [package="DIP (Dual Inline) [THT]"]
  R1 = Rotary Potentiometer (Large) [maximum_resistance=100kΩ knob_status=50% power=0.5W package=THT]

nets:
  N1: SAMD1.GND, R1.leg1

notes:
  Volume Rotary Pot

custom parts:
  XIAO SAMD21(Seeeduino): XIAO SAMD21 powered by Microchip SAMD21G18 chip is an ultra-small, high-performance universal development board, the pioneering product of the XIAO series. It supports Arduino / Micropython / CircuitPython development, which is the perfect microcontroller for you to get started with electronics.
